# Fritzing sketch temperaturedisplay (saved by Fritzing 0.9.1b)
breadboards: 1

parts:
  Composant1 = Arduino Uno (Rev3)
  R1 = PHOTOCELL [package=photocell-kit]
  U1 = 7-SEGMENT-4DIGIT-YOUNGSUN [package=7-segment-4digit-youngsun-longpads]
  R3 = Temperature Sensor (Thermistor) [package=THT]
  R4 = Resistor [tolerance=±5% resistance=10k package=THT]
  R5 = Resistor [tolerance=±5% resistance=4.7k package=THT]

nets:
  N1: Composant1.A0, U1.E
  N2: Composant1.A1, U1.A
  N3: Composant1.A4/SDA, R1.P$1, R4.Pin_1
  N4: Composant1.A5/SCL, R3.pin_0, R5.Pin_1
  N5: Composant1.D8, U1.G
  N6: Composant1.D9_PWM, U1.DIG3
  N7: Composant1.D10_PWM/SS, U1.DIG2
  N8: Composant1.D11_PWM/MOSI, U1.DIG1
  N9: Composant1.D12/MISO, U1.APOS-A
  N10: Composant1.D13/SCK, U1.APOS-C
  N11: Composant1.D3_PWM, U1.B
  N12: Composant1.D4, U1.C
  N13: Composant1.D5_PWM, U1.D
  N14: Composant1.D6_PWM, U1.DIG4
  N15: Composant1.D7, U1.F
  N16: Composant1.5V, R1.P$2, R3.pin_1
  N17: Composant1.GND, R4.Pin_0, R5.Pin_0

custom parts:
  Temperature Sensor (Thermistor): A 4.7k NTC Thermistor (Temperature Sensor)
